# Fritzing sketch 8x8x8x (saved by Fritzing 0.9.3b)
circuit board: 15cm x 10cm

parts:
  Part1 = Arduino Nano (Rev3.0) (ICSP)
  U1 = 74HC595 [package="DIP16 [THT]"]
  U2 = 74HC595 [package="DIP16 [THT]"]
  U3 = 74HC595 [package="DIP16 [THT]"]
  R2 = Resistor [tolerance=±5% resistance=220 package=THT]
  JP1 = Header 1 [package=1x01_offset]
  JP2 = Header 1 [package=1x01_offset]
  JP3 = Header 1 [package=1x01_offset]
  JP4 = Header 1 [package=1x01_offset]
  JP5 = Header 1 [package=1x01_offset]
  JP6 = Header 1 [package=1x01_offset]
  JP7 = Header 1 [package=1x01_offset]
  JP8 = Header 1 [package=1x01_offset]
  JP9 = Header 1 [package=1x01_offset]
  JP10 = Header 1 [package=1x01_offset]
  JP11 = Header 1 [package=1x01_offset]
  JP12 = Header 1 [package=1x01_offset]
  JP13 = Header 1 [package=1x01_offset]
  JP14 = Header 1 [package=1x01_offset]
  JP15 = Header 1 [package=1x01_offset]
  JP16 = Header 1 [package=1x01_offset]
  JP17 = Header 1 [package=1x01_offset]
  JP18 = Header 1 [package=1x01_offset]
  JP19 = Header 1 [package=1x01_offset]
  JP20 = Header 1 [package=1x01_offset]
  R3 = Resistor [tolerance=±5% resistance=220 package=THT]
  R4 = Resistor [tolerance=±5% resistance=220 package=THT]
  R6 = Resistor [tolerance=±5% resistance=220 package=THT]
  R7 = Resistor [tolerance=±5% resistance=220 package=THT]
  R8 = Resistor [tolerance=±5% resistance=220 package=THT]
  R9 = Resistor [tolerance=±5% resistance=220 package=THT]
  R10 = Resistor [tolerance=±5% resistance=220 package=THT]
  R11 = Resistor [tolerance=±5% resistance=220 package=THT]
  R12 = Resistor [tolerance=±5% resistance=220 package=THT]
  R14 = Resistor [tolerance=±5% resistance=220 package=THT]
  R15 = Resistor [tolerance=±5% resistance=220 package=THT]
  R16 = Resistor [tolerance=±5% resistance=220 package=THT]
  R17 = Resistor [tolerance=±5% resistance=220 package=THT]
  R18 = Resistor [tolerance=±5% resistance=220 package=THT]
  R19 = Resistor [tolerance=±5% resistance=220 package=THT]
  ULN2803 = ULN2803 Darlington Array
  U4 = 74HC595 [package="DIP16 [THT]"]
  R20 = Resistor [tolerance=±5% resistance=220 package=THT]
  R21 = Resistor [tolerance=±5% resistance=220 package=THT]
  R22 = Resistor [tolerance=±5% resistance=220 package=THT]
  R23 = Resistor [tolerance=±5% resistance=220 package=THT]
  R24 = Resistor [tolerance=±5% resistance=220 package=THT]
  R25 = Resistor [tolerance=±5% resistance=220 package=THT]
  R26 = Resistor [tolerance=±5% resistance=220 package=THT]
  R27 = Resistor [tolerance=±5% resistance=220 package=THT]
  JP21 = Header 1 [package=1x01_offset]
  JP22 = Header 1 [package=1x01_offset]
  JP23 = Header 1 [package=1x01_offset]
  JP24 = Header 1 [package=1x01_offset]
  JP25 = Header 1 [package=1x01_offset]
  JP26 = Header 1 [package=1x01_offset]
  JP27 = Header 1 [package=1x01_offset]
  JP28 = Header 1 [package=1x01_offset]
  JP29 = Header 1 [package=1x01_offset]
  JP30 = Header 1 [package=1x01_offset]
  JP31 = Header 1 [package=1x01_offset]
  JP32 = Header 1 [package=1x01_offset]
  U5 = 74HC595 [package="DIP16 [THT]"]
  R28 = Resistor [tolerance=±5% resistance=220 package=THT]
  R29 = Resistor [tolerance=±5% resistance=220 package=THT]
  R30 = Resistor [tolerance=±5% resistance=220 package=THT]
  R31 = Resistor [tolerance=±5% resistance=220 package=THT]
  R32 = Resistor [tolerance=±5% resistance=220 package=THT]
  R33 = Resistor [tolerance=±5% resistance=220 package=THT]
  R34 = Resistor [tolerance=±5% resistance=220 package=THT]
  R35 = Resistor [tolerance=±5% resistance=220 package=THT]
  JP33 = Header 1 [package=1x01_offset]
  JP34 = Header 1 [package=1x01_offset]
  JP35 = Header 1 [package=1x01_offset]
  JP36 = Header 1 [package=1x01_offset]
  JP37 = Header 1 [package=1x01_offset]
  JP38 = Header 1 [package=1x01_offset]
  JP39 = Header 1 [package=1x01_offset]
  JP40 = Header 1 [package=1x01_offset]
  U6 = 74HC595 [package="DIP16 [THT]"]
  R36 = Resistor [tolerance=±5% resistance=220 package=THT]
  R37 = Resistor [tolerance=±5% resistance=220 package=THT]
  R38 = Resistor [tolerance=±5% resistance=220 package=THT]
  R39 = Resistor [tolerance=±5% resistance=220 package=THT]
  R40 = Resistor [tolerance=±5% resistance=220 package=THT]
  R41 = Resistor [tolerance=±5% resistance=220 package=THT]
  R42 = Resistor [tolerance=±5% resistance=220 package=THT]
  R43 = Resistor [tolerance=±5% resistance=220 package=THT]
  JP41 = Header 1 [package=1x01_offset]
  JP42 = Header 1 [package=1x01_offset]
  JP43 = Header 1 [package=1x01_offset]
  JP44 = Header 1 [package=1x01_offset]
  JP45 = Header 1 [package=1x01_offset]
  JP46 = Header 1 [package=1x01_offset]
  JP47 = Header 1 [package=1x01_offset]
  JP48 = Header 1 [package=1x01_offset]
  U7 = 74HC595 [package="DIP16 [THT]"]
  R44 = Resistor [tolerance=±5% resistance=220 package=THT]
  R45 = Resistor [tolerance=±5% resistance=220 package=THT]
  R46 = Resistor [tolerance=±5% resistance=220 package=THT]
  R47 = Resistor [tolerance=±5% resistance=220 package=THT]
  R48 = Resistor [tolerance=±5% resistance=220 package=THT]
  R49 = Resistor [tolerance=±5% resistance=220 package=THT]
  R50 = Resistor [tolerance=±5% resistance=220 package=THT]
  R51 = Resistor [tolerance=±5% resistance=220 package=THT]
  JP49 = Header 1 [package=1x01_offset]
  JP50 = Header 1 [package=1x01_offset]
  JP51 = Header 1 [package=1x01_offset]
  JP52 = Header 1 [package=1x01_offset]
  JP53 = Header 1 [package=1x01_offset]
  JP54 = Header 1 [package=1x01_offset]
  JP55 = Header 1 [package=1x01_offset]
  JP56 = Header 1 [package=1x01_offset]
  U8 = 74HC595 [package="DIP16 [THT]"]
  R52 = Resistor [tolerance=±5% resistance=220 package=THT]
  R53 = Resistor [tolerance=±5% resistance=220 package=THT]
  R54 = Resistor [tolerance=±5% resistance=220 package=THT]
  R55 = Resistor [tolerance=±5% resistance=220 package=THT]
  R56 = Resistor [tolerance=±5% resistance=220 package=THT]
  R57 = Resistor [tolerance=±5% resistance=220 package=THT]
  R58 = Resistor [tolerance=±5% resistance=220 package=THT]
  R59 = Resistor [tolerance=±5% resistance=220 package=THT]
  JP57 = Header 1 [package=1x01_offset]
  JP58 = Header 1 [package=1x01_offset]
  JP59 = Header 1 [package=1x01_offset]
  JP60 = Header 1 [package=1x01_offset]
  JP61 = Header 1 [package=1x01_offset]
  JP62 = Header 1 [package=1x01_offset]
  JP63 = Header 1 [package=1x01_offset]
  JP64 = Header 1 [package=1x01_offset]
  U9 = 74HC595 [package="DIP16 [THT]"]
  R60 = Resistor [tolerance=±5% resistance=220 package=THT]
  R61 = Resistor [tolerance=±5% resistance=220 package=THT]
  R62 = Resistor [tolerance=±5% resistance=220 package=THT]
  R63 = Resistor [tolerance=±5% resistance=220 package=THT]
  R64 = Resistor [tolerance=±5% resistance=220 package=THT]
  R65 = Resistor [tolerance=±5% resistance=220 package=THT]
  R66 = Resistor [tolerance=±5% resistance=220 package=THT]
  R67 = Resistor [tolerance=±5% resistance=220 package=THT]
  JP65 = Header 1 [package=1x01_offset]
  JP66 = Header 1 [package=1x01_offset]
  JP67 = Header 1 [package=1x01_offset]
  JP68 = Header 1 [package=1x01_offset]
  JP69 = Header 1 [package=1x01_offset]
  JP70 = Header 1 [package=1x01_offset]
  JP71 = Header 1 [package=1x01_offset]
  JP72 = Header 1 [package=1x01_offset]
  J1 = screw terminal, 2 pins
  C1 = Electrolytic Capacitor [capacitance=10µF package="200 mil [THT, electrolytic]"]

nets:
  GND: Part1.GND, U1.GND, U2.GND, U3.GND, ULN2803.GND, U4.GND, U5.GND, U6.GND, U7.GND, U8.GND, U9.GND, J1.pin1, C1.-
  N1: Part1.D9, U1.ST_CP, U2.ST_CP, U3.ST_CP, U4.ST_CP, U5.ST_CP, U6.ST_CP, U7.ST_CP, U8.ST_CP, U9.ST_CP
  N2: Part1.D10, U1.OE, U2.OE, U3.OE, U4.OE, U5.OE, U6.OE, U7.OE, U8.OE, U9.OE
  N3: Part1.D11/MOSI, U1.DS
  VCC: Part1.5V, U1.MR, U1.VCC, U2.MR, U2.VCC, U3.MR, U3.VCC, ULN2803.COMMON, U4.MR, U4.VCC, U5.MR, U5.VCC, U6.MR, U6.VCC, U7.MR, U7.VCC, U8.MR, U8.VCC, U9.MR, U9.VCC, J1.pin2, C1.+
  N4: Part1.D13/SCK, U1.SH_CP, U2.SH_CP, U3.SH_CP, U4.SH_CP, U5.SH_CP, U6.SH_CP, U7.SH_CP, U8.SH_CP, U9.SH_CP
  N5: U1.Q1, ULN2803.I7
  N6: U1.Q2, ULN2803.I6
  N7: U1.Q3, ULN2803.I5
  N8: U1.Q4, ULN2803.I4
  N9: U1.Q5, ULN2803.I3
  N10: U1.Q6, ULN2803.I2
  N11: U1.Q7, ULN2803.I1
  N12: U1.Q7', U3.DS
  N13: U1.Q0, ULN2803.I8
  N14: U2.Q1, R12.Pin_0
  N15: U2.Q2, R11.Pin_0
  N16: U2.Q3, R10.Pin_0
  N17: U2.Q4, R9.Pin_0
  N18: U2.Q5, R8.Pin_0
  N19: U2.Q6, R7.Pin_0
  N20: U2.Q7, R6.Pin_0
  N21: U2.Q7', U4.DS
  N22: U2.DS, U3.Q7'
  N23: U2.Q0, R3.Pin_0
  N24: U3.Q1, R4.Pin_0
  N25: U3.Q2, R19.Pin_0
  N26: U3.Q3, R18.Pin_0
  N27: U3.Q4, R17.Pin_0
  N28: U3.Q5, R16.Pin_0
  N29: U3.Q6, R15.Pin_0
  N30: U3.Q7, R14.Pin_0
  N31: U3.Q0, R2.Pin_0
  N32: R2.Pin_1, JP9.1
  N33: JP1.1, ULN2803.O5
  N34: JP2.1, ULN2803.O7
  N35: JP3.1, ULN2803.O6
  N36: JP4.1, ULN2803.O8
  N37: JP5.1, R18.Pin_1
  N38: JP6.1, R17.Pin_1
  N39: JP7.1, R4.Pin_1
  N40: JP8.1, R19.Pin_1
  N41: JP10.1, R16.Pin_1
  N42: JP11.1, R14.Pin_1
  N43: JP12.1, R15.Pin_1
  N44: JP13.1, R7.Pin_1
  N45: JP14.1, R8.Pin_1
  N46: JP15.1, R3.Pin_1
  N47: JP16.1, R6.Pin_1
  N48: JP17.1, R10.Pin_1
  N49: JP18.1, R11.Pin_1
  N50: JP19.1, R9.Pin_1
  N51: JP20.1, R12.Pin_1
  N52: ULN2803.O4, JP29.1
  N53: ULN2803.O3, JP31.1
  N54: ULN2803.O2, JP30.1
  N55: ULN2803.O1, JP32.1
  N56: U4.Q1, R20.Pin_0
  N57: U4.Q2, R21.Pin_0
  N58: U4.Q3, R22.Pin_0
  N59: U4.Q4, R23.Pin_0
  N60: U4.Q5, R24.Pin_0
  N61: U4.Q6, R25.Pin_0
  N62: U4.Q7, R26.Pin_0
  N63: U4.Q7', U5.DS
  N64: U4.Q0, R27.Pin_0
  N65: R20.Pin_1, JP21.1
  N66: R21.Pin_1, JP23.1
  N67: R22.Pin_1, JP24.1
  N68: R23.Pin_1, JP22.1
  N69: R24.Pin_1, JP27.1
  N70: R25.Pin_1, JP28.1
  N71: R26.Pin_1, JP25.1
  N72: R27.Pin_1, JP26.1
  N73: U5.Q1, R28.Pin_0
  N74: U5.Q2, R29.Pin_0
  N75: U5.Q3, R30.Pin_0
  N76: U5.Q4, R31.Pin_0
  N77: U5.Q5, R32.Pin_0
  N78: U5.Q6, R33.Pin_0
  N79: U5.Q7, R34.Pin_0
  N80: U5.Q7', U6.DS
  N81: U5.Q0, R35.Pin_0
  N82: R28.Pin_1, JP33.1
  N83: R29.Pin_1, JP35.1
  N84: R30.Pin_1, JP36.1
  N85: R31.Pin_1, JP34.1
  N86: R32.Pin_1, JP39.1
  N87: R33.Pin_1, JP40.1
  N88: R34.Pin_1, JP37.1
  N89: R35.Pin_1, JP38.1
  N90: U6.Q1, R36.Pin_0
  N91: U6.Q2, R37.Pin_0
  N92: U6.Q3, R38.Pin_0
  N93: U6.Q4, R39.Pin_0
  N94: U6.Q5, R40.Pin_0
  N95: U6.Q6, R41.Pin_0
  N96: U6.Q7, R42.Pin_0
  N97: U6.Q7', U7.DS
  N98: U6.Q0, R43.Pin_0
  N99: R36.Pin_1, JP41.1
  N100: R37.Pin_1, JP43.1
  N101: R38.Pin_1, JP44.1
  N102: R39.Pin_1, JP42.1
  N103: R40.Pin_1, JP47.1
  N104: R41.Pin_1, JP48.1
  N105: R42.Pin_1, JP45.1
  N106: R43.Pin_1, JP46.1
  N107: U7.Q1, R44.Pin_0
  N108: U7.Q2, R45.Pin_0
  N109: U7.Q3, R46.Pin_0
  N110: U7.Q4, R47.Pin_0
  N111: U7.Q5, R48.Pin_0
  N112: U7.Q6, R49.Pin_0
  N113: U7.Q7, R50.Pin_0
  N114: U7.Q7', U8.DS
  N115: U7.Q0, R51.Pin_0
  N116: R44.Pin_1, JP49.1
  N117: R45.Pin_1, JP51.1
  N118: R46.Pin_1, JP52.1
  N119: R47.Pin_1, JP50.1
  N120: R48.Pin_1, JP55.1
  N121: R49.Pin_1, JP56.1
  N122: R50.Pin_1, JP53.1
  N123: R51.Pin_1, JP54.1
  N124: U8.Q1, R52.Pin_0
  N125: U8.Q2, R53.Pin_0
  N126: U8.Q3, R54.Pin_0
  N127: U8.Q4, R55.Pin_0
  N128: U8.Q5, R56.Pin_0
  N129: U8.Q6, R57.Pin_0
  N130: U8.Q7, R58.Pin_0
  N131: U8.Q7', U9.DS
  N132: U8.Q0, R59.Pin_0
  N133: R52.Pin_1, JP57.1
  N134: R53.Pin_1, JP59.1
  N135: R54.Pin_1, JP60.1
  N136: R55.Pin_1, JP58.1
  N137: R56.Pin_1, JP63.1
  N138: R57.Pin_1, JP64.1
  N139: R58.Pin_1, JP61.1
  N140: R59.Pin_1, JP62.1
  N141: U9.Q1, R60.Pin_0
  N142: U9.Q2, R61.Pin_0
  N143: U9.Q3, R62.Pin_0
  N144: U9.Q4, R63.Pin_0
  N145: U9.Q5, R64.Pin_0
  N146: U9.Q6, R65.Pin_0
  N147: U9.Q7, R66.Pin_0
  N148: U9.Q0, R67.Pin_0
  N149: R60.Pin_1, JP65.1
  N150: R61.Pin_1, JP67.1
  N151: R62.Pin_1, JP68.1
  N152: R63.Pin_1, JP66.1
  N153: R64.Pin_1, JP71.1
  N154: R65.Pin_1, JP72.1
  N155: R66.Pin_1, JP69.1
  N156: R67.Pin_1, JP70.1

notes:
  -
  +++ 5V
  +++ 5V +++
  --- GND
  C
  C1
  USB
  C - 100nF
  74HC595
  ULN2803
  R1-R64 100-500 Ohm

custom parts:
  ULN2803 Darlington Array: ULN2803 Darlington Transistor Array with Flyback Protection
